# Fritzing sketch DrumRobot (saved by Fritzing 0.9.10b)
stripboards: 2

parts:
  DrumRobot = Arduino Uno (Rev3)
  HEAD = Basic Servo
  + = Screw terminal - 2 pins [package=THT]
  5V = Power plug
  GND = Screw terminal - 2 pins [package=THT]
  GND_2 = Screw terminal - 2 pins [package=THT]
  GND_3 = Screw terminal - 2 pins [package=THT]
  +_2 = Screw terminal - 2 pins [package=THT]
  BD = Basic Servo
  LEFT_HIT = Basic Servo
  RIGHT_HIT = Basic Servo
  HIPS = Basic Servo
  +_3 = Screw terminal - 2 pins [package=THT]
  RoboMaster = Arduino Uno (Rev3)

nets:
  N1: DrumRobot.A4/SDA, RoboMaster.A4/SDA
  N2: DrumRobot.A5/SCL, RoboMaster.A5/SCL
  N3: DrumRobot.D9_PWM, RIGHT_HIT.pulse
  N4: DrumRobot.D10_PWM/SS, HIPS.pulse
  GND: DrumRobot.GND, HEAD.gnd, 5V.GND, GND.pin1, GND.pin2, GND_2.pin1, GND_2.pin2, GND_3.pin1, GND_3.pin2, BD.gnd, LEFT_HIT.gnd, RIGHT_HIT.gnd, HIPS.gnd, RoboMaster.GND
  N5: DrumRobot.D3_PWM, HEAD.pulse
  N6: DrumRobot.D5_PWM, BD.pulse
  N7: DrumRobot.D6_PWM, LEFT_HIT.pulse
  VCC: HEAD.vcc, +.pin1, +.pin2, 5V.VCC, +_2.pin1, +_2.pin2, BD.vcc, LEFT_HIT.vcc, RIGHT_HIT.vcc, HIPS.vcc, +_3.pin1, +_3.pin2

notes:
  HEAD
  BD
  LEFT HIT
  RIGHT HIT
  HIPS
  RoboMaster
  5V
  DrumRobot
