# Fritzing sketch GlockenRobot (saved by Fritzing 0.9.10b)
stripboards: 2

parts:
  GlockenRobot = Arduino Uno (Rev3)
  HEAD = Basic Servo
  + = Screw terminal - 2 pins [package=THT]
  5V = Power plug
  GND = Screw terminal - 2 pins [package=THT]
  GND_2 = Screw terminal - 2 pins [package=THT]
  GND_3 = Screw terminal - 2 pins [package=THT]
  +_2 = Screw terminal - 2 pins [package=THT]
  LEFT_HIT = Basic Servo
  RIGHT_HIT = Basic Servo
  LEFT_POS = Basic Servo
  RIGHT_POS = Basic Servo
  +_3 = Screw terminal - 2 pins [package=THT]
  RoboMaster = Arduino Uno (Rev3)

nets:
  N1: GlockenRobot.A4/SDA, RoboMaster.A4/SDA
  N2: GlockenRobot.A5/SCL, RoboMaster.A5/SCL
  N3: GlockenRobot.D9_PWM, LEFT_POS.pulse
  N4: GlockenRobot.D10_PWM/SS, RIGHT_POS.pulse
  GND: GlockenRobot.GND, HEAD.gnd, 5V.GND, GND.pin1, GND.pin2, GND_2.pin1, GND_2.pin2, GND_3.pin1, GND_3.pin2, LEFT_HIT.gnd, RIGHT_HIT.gnd, LEFT_POS.gnd, RIGHT_POS.gnd, RoboMaster.GND
  N5: GlockenRobot.D3_PWM, HEAD.pulse
  N6: GlockenRobot.D5_PWM, LEFT_HIT.pulse
  N7: GlockenRobot.D6_PWM, RIGHT_HIT.pulse
  VCC: HEAD.vcc, +.pin1, +.pin2, 5V.VCC, +_2.pin1, +_2.pin2, LEFT_HIT.vcc, RIGHT_HIT.vcc, LEFT_POS.vcc, RIGHT_POS.vcc, +_3.pin1, +_3.pin2

notes:
  HEAD
  LEFT HIT
  RIGHT HIT
  LEFT POS
  RIGHT POS
  RoboMaster
  5V
  GlockenRobot
