# Fritzing sketch RoboMaster (saved by Fritzing 0.9.10b)
perfboards: 1
stripboards: 1

parts:
  RoboMaster = Arduino Uno (Rev3)
  Optocoupler = IC, DIP package, 8 pins [chip_label=IC]
  MIDI_IN = DIN-5 jack (MIDI) [package=THT]
  R1 = Resistor [tolerance=±5% power=0.25 resistance=220 package=THT]
  D1 = Rectifier Diode [part_number=1N4001 package="300 mil [THT]"]
  R2 = Resistor [tolerance=±5% power=0.25 resistance=220 package=THT]
  R3 = Resistor [tolerance=±5% power=0.25 resistance=4.7k package=THT]
  J6 = Screw terminal - 2 pins [package=THT]
  J7 = Screw terminal - 2 pins [package=THT]
  J8 = Screw terminal - 2 pins [package=THT]
  J9 = Screw terminal - 2 pins [package=THT]
  J10 = Screw terminal - 2 pins [package=THT]
  J11 = Screw terminal - 2 pins [package=THT]
  J12 = Screw terminal - 2 pins [package=THT]
  J13 = Screw terminal - 2 pins [package=THT]
  J14 = Screw terminal - 2 pins [package=THT]
  J15 = Screw terminal - 2 pins [package=THT]
  J16 = Screw terminal - 2 pins [package=THT]
  J17 = Screw terminal - 2 pins [package=THT]

nets:
  N1: RoboMaster.A4/SDA, J10.pin1, J10.pin2, J11.pin1, J11.pin2, J12.pin1, J12.pin2, J13.pin1, J13.pin2
  N2: RoboMaster.A5/SCL, J6.pin1, J6.pin2, J7.pin1, J7.pin2, J8.pin1, J8.pin2, J9.pin1, J9.pin2
  N3: RoboMaster.GND, Optocoupler.pin5, R3.Pin_0, J14.pin1, J14.pin2, J15.pin1, J15.pin2, J16.pin1, J16.pin2, J17.pin1, J17.pin2
  N4: RoboMaster.D0/RX, Optocoupler.pin6, R2.Pin_0
  N5: RoboMaster.5V, Optocoupler.pin8, R2.Pin_1
  N6: Optocoupler.pin2, R1.Pin_1, D1.cathode
  N7: Optocoupler.pin3, MIDI_IN.5, D1.anode
  N8: Optocoupler.pin7, R3.Pin_1
  N9: MIDI_IN.4, R1.Pin_0

notes:
  RoboMaster
  to other arduinos
  MIDI in
